// Logisim project 1to4demux.circ as structural Verilog: 1 circuit, main circuit main
module main (
  input  s0,
  input  s1,
  input  A,
  output out_4,
  output out_5,
  output out_6,
  output out_7
);

  wire and_1_out, and_2_out, and_3_out, and_4_out, not_1_out, not_2_out;

  not not_1 (not_1_out, s0);
  not not_2 (not_2_out, s1);
  and and_1 (and_1_out, A, not_2_out);
  and and_2 (and_2_out, not_1_out, s1);
  and and_3 (and_3_out, s0, not_2_out);
  and and_4 (and_4_out, s0, s1);
  and and_5 (out_4, and_1_out, not_1_out);
  and and_6 (out_5, and_2_out, s1);
  and and_7 (out_6, and_3_out, A);
  and and_8 (out_7, and_4_out, A);
endmodule
