// Logisim project 4 bit sync up counter.circ as structural Verilog: 1 circuit, main circuit 4-bit Counter
module _4_bit_Counter (
  input  Clock,
  input  Clear,
  output Q0,
  output Q1,
  output Q2,
  output Q3
);

  wire AND_2_out, AND_out;

  J_K_Flip_Flop F_F_A (.J(1'b1), .clk(Clock), .K(1'b1), .Q(Q0), .reset(Clear));  // open: Qn, preset, en
  J_K_Flip_Flop F_F_B (.J(Q0), .clk(Clock), .K(Q0), .Q(Q1), .reset(Clear));  // open: Qn, preset, en
  and AND (AND_out, Q1, Q0);
  J_K_Flip_Flop F_F_C (.J(AND_out), .clk(Clock), .K(AND_out), .Q(Q2), .reset(Clear));  // open: Qn, preset, en
  and AND_2 (AND_2_out, Q2, AND_out);
  J_K_Flip_Flop F_F_D (.J(AND_2_out), .clk(Clock), .K(AND_2_out), .Q(Q3), .reset(Clear));  // open: Qn, preset, en

  // Notes on the sheet:
  //   4-bit Synchronous Up Counter
endmodule
