// Logisim project 4to1mux.circ as structural Verilog: 1 circuit, main circuit main
module main (
  input  A,
  input  B,
  input  C,
  input  in_4,
  input  s0,
  input  s1,
  output out_7
);

  wire AND1_out, AND2_out, AND3_out, AND4_out, AND5_out, AND6_out, AND7_out, AND8_out, not_1_out, not_2_out,
       or_1_out, or_2_out;

  not not_1 (not_1_out, s0);
  not not_2 (not_2_out, s1);
  and AND1 (AND1_out, A, not_1_out);
  and AND3 (AND3_out, B, not_1_out);
  and AND5 (AND5_out, C, not_2_out);
  and AND7 (AND7_out, in_4, s0);
  and AND2 (AND2_out, AND1_out, not_2_out);
  and AND4 (AND4_out, AND3_out, s1);
  and AND6 (AND6_out, AND5_out, s0);
  and AND8 (AND8_out, AND7_out, s1);
  or or_1 (or_1_out, AND2_out, AND4_out);
  or or_2 (or_2_out, AND6_out, AND8_out);
  or or_3 (out_7, or_1_out, or_2_out);

  // Notes on the sheet:
  //   SELECT LINES s0 AND s1 ARE USED TO SELECT THE INPUTS
  //   INPUT LINES A,B,C,D
  //   4 TO 1 MULTIPLEXER USING BASIC GATES
endmodule
