// Logisim project ExamCheatsheet.circ as structural Verilog: 17 circuits, main circuit Look-ahead Carry Generator
module main (
  input  [3:0] X,
  input  [3:0] Y,
  output [3:0] SUM_in_2_s_Complement,
  output [3:0] SUM_in_Signed_Magnitude
);

  wire clock_1_out;
  wire [3:0] _2_s_Complement_2__2x, _2_s_Complement_3__2x, _2_s_Complement__2x, multiplexer_1_out,
       multiplexer_2_out;

  Clock clock_1 (.out(clock_1_out));
  _2_s_Complement _2_s_Complement (.X({1'b0, X[2:0]}), .Clock(clock_1_out), ._2X(_2_s_Complement__2x));
  _2_s_Complement _2_s_Complement_2 (.X({1'b0, Y[2:0]}), .Clock(clock_1_out), ._2X(_2_s_Complement_2__2x));
  Multiplexer #(.width(4)) multiplexer_1 (
    .in0(X), .in1(_2_s_Complement__2x), .out(multiplexer_1_out), .sel(X[3]));  // open: en
  Multiplexer #(.width(4)) multiplexer_2 (
    .in0(Y), .in1(_2_s_Complement_2__2x), .out(multiplexer_2_out), .sel(Y[3]));  // open: en
  Parallel_Adder Parallel_Adder (
    .A(multiplexer_1_out), .Clock(clock_1_out), .B(multiplexer_2_out), .SUM(SUM_in_2_s_Complement));  // open: C
  _2_s_Complement _2_s_Complement_3 (
    .X({1'b0, SUM_in_2_s_Complement[2:0]}), .Clock(clock_1_out), ._2X(_2_s_Complement_3__2x));
  Multiplexer #(.width(4)) multiplexer_3 (
    .in0(SUM_in_2_s_Complement), .in1(_2_s_Complement_3__2x), .out(SUM_in_Signed_Magnitude),
    .sel(SUM_in_2_s_Complement[3]));  // open: en
endmodule

module _2_s_Complement (
  input  [3:0] X,
  input  Clock,
  output [3:0] _2X
);

  wire [0:0] not_1_out;
  wire [3:0] not_2_out;

  not not_1 (not_1_out[0], 1'b0);
  not not_2 (not_2_out[0], X[0]);
  not not_3 (not_2_out[1], X[1]);
  not not_4 (not_2_out[2], X[2]);
  not not_5 (not_2_out[3], X[3]);
  Parallel_Adder parallel_adder_1 (.A(not_2_out), .Clock(Clock), .B({3'b000, not_1_out[0]}), .SUM(_2X));  // open: C
endmodule

module Parallel_Adder (
  input  [3:0] A,
  input  Clock,
  input  [3:0] B,
  output [3:0] SUM,
  output C
);

  wire full_adder_1_c, full_adder_2_c, half_adder_1_c, PIPO_Shift_Register_2_q0, PIPO_Shift_Register_2_q1,
       PIPO_Shift_Register_2_q2, PIPO_Shift_Register_2_q3, PIPO_Shift_Register_q0, PIPO_Shift_Register_q1,
       PIPO_Shift_Register_q2, PIPO_Shift_Register_q3;

  PIPO_Shift_Register PIPO_Shift_Register (
    .Clock(Clock), .I3(A[3]), .I2(A[2]), .I1(A[1]), .I0(A[0]), .Q3(PIPO_Shift_Register_q3),
    .Q2(PIPO_Shift_Register_q2), .Q1(PIPO_Shift_Register_q1), .Q0(PIPO_Shift_Register_q0));
  PIPO_Shift_Register PIPO_Shift_Register_2 (
    .Clock(Clock), .I3(B[3]), .I2(B[2]), .I1(B[1]), .I0(B[0]), .Q3(PIPO_Shift_Register_2_q3),
    .Q2(PIPO_Shift_Register_2_q2), .Q1(PIPO_Shift_Register_2_q1), .Q0(PIPO_Shift_Register_2_q0));
  Half_Adder half_adder_1 (.X(PIPO_Shift_Register_q0), .Y(PIPO_Shift_Register_2_q0), .S(SUM[0]), .C(half_adder_1_c));
  Full_Adder full_adder_1 (
    .C_IN(half_adder_1_c), .X(PIPO_Shift_Register_q1), .Y(PIPO_Shift_Register_2_q1), .S(SUM[1]),
    .C(full_adder_1_c));
  Full_Adder full_adder_2 (
    .C_IN(full_adder_1_c), .X(PIPO_Shift_Register_q2), .Y(PIPO_Shift_Register_2_q2), .S(SUM[2]),
    .C(full_adder_2_c));
  Full_Adder full_adder_3 (
    .C_IN(full_adder_2_c), .X(PIPO_Shift_Register_q3), .Y(PIPO_Shift_Register_2_q3), .S(SUM[3]), .C(C));
endmodule

module PIPO_Shift_Register (
  input  I3,
  input  I2,
  input  I1,
  input  I0,
  input  Clock,
  output Q3,
  output Q2,
  output Q1,
  output Q0
);

  D_Flip_Flop F_F_3 (.clk(Clock), .D(I3), .Q(Q3));  // open: Qn, preset, en, reset
  D_Flip_Flop F_F_2 (.clk(Clock), .D(I2), .Q(Q2));  // open: Qn, preset, en, reset
  D_Flip_Flop F_F_1 (.clk(Clock), .D(I1), .Q(Q1));  // open: Qn, preset, en, reset
  D_Flip_Flop F_F_0 (.clk(Clock), .D(I0), .Q(Q0));  // open: Qn, preset, en, reset
endmodule

module _4_bit_Counter (
  input  Clock,
  input  Clear,
  output Q0,
  output Q1,
  output Q2,
  output Q3
);

  wire AND_2_out, AND_out, NOT_out;

  not NOT (NOT_out, 1'b0);
  J_K_Flip_Flop F_F_A (.J(NOT_out), .clk(Clock), .K(NOT_out), .Q(Q0), .reset(Clear));  // open: Qn, preset, en
  J_K_Flip_Flop F_F_B (.J(Q0), .clk(Clock), .K(Q0), .Q(Q1), .reset(Clear));  // open: Qn, preset, en
  and AND (AND_out, Q1, Q0);
  J_K_Flip_Flop F_F_C (.J(AND_out), .clk(Clock), .K(AND_out), .Q(Q2), .reset(Clear));  // open: Qn, preset, en
  and AND_2 (AND_2_out, Q2, AND_out);
  J_K_Flip_Flop F_F_D (.J(AND_2_out), .clk(Clock), .K(AND_2_out), .Q(Q3), .reset(Clear));  // open: Qn, preset, en

  // Notes on the sheet:
  //   4-bit Synchronous Up Counter
endmodule

// FA
module Full_Adder (
  input  C_IN,
  input  X,
  input  Y,
  output S,
  output C
);

  wire Half_Adder_2_c, Half_Adder_c, Half_Adder_s;

  Half_Adder Half_Adder (.X(X), .Y(Y), .S(Half_Adder_s), .C(Half_Adder_c));
  Half_Adder Half_Adder_2 (.X(C_IN), .Y(Half_Adder_s), .S(S), .C(Half_Adder_2_c));
  OR or_1 (.X(Half_Adder_2_c), .Y(Half_Adder_c), .S(C));
endmodule

// HA
module Half_Adder (
  input  X,
  input  Y,
  output S,
  output C
);

  XOR xor_1 (.X(X), .Y(Y), .XOR(S));
  AND and_1 (.X(X), .Y(Y), .S(C));
endmodule

module Look_ahead_Carry_Generator (
  input  Ai,
  input  Bi,
  input  Ci,
  output Si,
  output Ci_2
);

  wire and_1_s, and_2_s, xor_1_xor;

  XOR xor_1 (.X(Ai), .Y(Bi), .XOR(xor_1_xor));
  AND and_1 (.X(Bi), .Y(Ai), .S(and_1_s));
  XOR xor_2 (.X(xor_1_xor), .Y(Ci), .XOR(Si));
  AND and_2 (.X(xor_1_xor), .Y(Ci), .S(and_2_s));
  OR or_1 (.X(and_2_s), .Y(and_1_s), .S(Ci_2));
endmodule

module _3_bit_Magnitude_Comparator (
  input  [2:0] A,
  input  [2:0] B,
  output A___B,
  output A___B_2,
  output A___B_3
);

  wire and_1_s, and_2_s, and_3_s, and_4_s, and_5_s, and_6_s, and_7_s, and_8_s, n3_input_and_1_and,
       n3_input_and_2_and, nor_1_s, nor_2_s, nor_3_s, not_1_out, not_2_out, not_3_out, not_4_out, not_5_out,
       not_6_out;

  not not_1 (not_1_out, A[2]);
  not not_2 (not_2_out, B[2]);
  not not_3 (not_3_out, A[1]);
  not not_4 (not_4_out, B[1]);
  not not_5 (not_5_out, A[0]);
  not not_6 (not_6_out, B[0]);
  AND and_1 (.X(not_1_out), .Y(B[2]), .S(and_1_s));
  AND and_2 (.X(A[2]), .Y(not_2_out), .S(and_2_s));
  AND and_3 (.X(not_3_out), .Y(B[1]), .S(and_3_s));
  AND and_4 (.X(A[1]), .Y(not_4_out), .S(and_4_s));
  AND and_5 (.X(not_5_out), .Y(B[0]), .S(and_5_s));
  AND and_6 (.X(A[0]), .Y(not_6_out), .S(and_6_s));
  NOR nor_1 (.X(and_1_s), .Y(and_2_s), .S(nor_1_s));
  NOR nor_2 (.X(and_3_s), .Y(and_4_s), .S(nor_2_s));
  NOR nor_3 (.X(and_5_s), .Y(and_6_s), .S(nor_3_s));
  AND and_7 (.X(nor_1_s), .Y(and_3_s), .S(and_7_s));
  AND and_8 (.X(and_4_s), .Y(nor_1_s), .S(and_8_s));
  _3_input_AND u_3_input_and_1 (.A(nor_2_s), .B(and_5_s), .C(nor_1_s), .AND(n3_input_and_1_and));
  _3_input_AND u_3_input_and_2 (.A(nor_2_s), .B(and_6_s), .C(nor_1_s), .AND(n3_input_and_2_and));
  _3_input_OR u_3_input_or_1 (.A(and_1_s), .B(and_7_s), .C(n3_input_and_1_and), .OR(A___B));
  _3_input_OR u_3_input_or_2 (.A(and_2_s), .B(and_8_s), .C(n3_input_and_2_and), .OR(A___B_2));
  _3_input_AND u_3_input_and_3 (.A(nor_1_s), .B(nor_2_s), .C(nor_3_s), .AND(A___B_3));
endmodule

module XOR (
  input  X,
  input  Y,
  output XOR
);

  wire nand_1_out, nand_2_out, nand_3_out, nand_4_out;

  nand nand_1 (nand_1_out, X, X);
  nand nand_2 (nand_2_out, Y, Y);
  nand nand_3 (nand_3_out, nand_1_out, Y);
  nand nand_4 (nand_4_out, X, nand_2_out);
  nand nand_5 (XOR, nand_3_out, nand_4_out);
endmodule

module AND (
  input  X,
  input  Y,
  output S
);

  wire nand_1_out;

  nand nand_1 (nand_1_out, X, Y);
  nand nand_2 (S, nand_1_out, nand_1_out);
endmodule

module OR (
  input  X,
  input  Y,
  output S
);

  wire nand_1_out, nand_2_out;

  nand nand_1 (nand_1_out, X, X);
  nand nand_2 (nand_2_out, Y, Y);
  nand nand_3 (S, nand_1_out, nand_2_out);
endmodule

module NOR (
  input  X,
  input  Y,
  output S
);

  wire or_1_s;

  OR or_1 (.X(X), .Y(Y), .S(or_1_s));
  nand nand_1 (S, or_1_s, or_1_s);
endmodule

// OR
module _3_input_OR (
  input  A,
  input  B,
  input  C,
  output OR
);

  wire or_1_s;

  OR or_1 (.X(A), .Y(B), .S(or_1_s));
  OR or_2 (.X(or_1_s), .Y(C), .S(OR));
endmodule

// AND
module _3_input_AND (
  input  A,
  input  B,
  input  C,
  output AND
);

  wire and_1_s;

  AND and_1 (.X(A), .Y(B), .S(and_1_s));
  AND and_2 (.X(and_1_s), .Y(C), .S(AND));
endmodule

module _3_input_XOR (
  input  A,
  input  B,
  input  C,
  output XOR
);

  wire xor_1_xor;

  XOR xor_1 (.X(A), .Y(B), .XOR(xor_1_xor));
  XOR xor_2 (.X(C), .Y(xor_1_xor), .XOR(XOR));
endmodule

// NAND
module _3_input_NAND (
  input  A,
  input  B,
  input  C,
  output NAND
);

  wire and_1_s, and_2_s;

  AND and_1 (.X(A), .Y(B), .S(and_1_s));
  AND and_2 (.X(and_1_s), .Y(C), .S(and_2_s));
  not not_1 (NAND, and_2_s);
endmodule
