// Logisim project bcd ripple counter.circ as structural Verilog: 1 circuit, main circuit main
module main (
  output Q0,
  output Q1,
  output Q2,
  output Q3
);

  wire AND_out, clock_out, not_1_out, not_2_out;

  Clock clock (.out(clock_out));
  J_K_Flip_Flop #(.trigger("falling")) j_k_ff_1 (
    .J(1'b1), .clk(clock_out), .K(1'b1), .Q(Q0), .reset(AND_out));  // open: Qn, preset, en
  J_K_Flip_Flop #(.trigger("falling")) j_k_ff_2 (
    .J(1'b1), .clk(Q0), .K(1'b1), .Q(Q1), .reset(AND_out));  // open: Qn, preset, en
  J_K_Flip_Flop #(.trigger("falling")) j_k_ff_3 (
    .J(1'b1), .clk(Q1), .K(1'b1), .Q(Q2), .reset(AND_out));  // open: Qn, preset, en
  J_K_Flip_Flop #(.trigger("falling")) j_k_ff_4 (
    .J(1'b1), .clk(Q2), .K(1'b1), .Q(Q3), .reset(AND_out));  // open: Qn, preset, en
  not not_1 (not_1_out, Q0);
  not not_2 (not_2_out, Q2);
  and AND (AND_out, not_1_out, Q1, not_2_out, Q3);
endmodule
