// Logisim project bcdTOdecimalDecoder.circ as structural Verilog: 1 circuit, main circuit main
module main (
  input  w,
  input  x,
  input  y,
  input  z,
  output out_5,
  output out_6,
  output out_7,
  output out_8,
  output out_9,
  output out_10,
  output out_11,
  output out_12,
  output out_13,
  output out_14
);

  wire and9_out, and10_out, and11_out, and12_out, and13_out, and14_out, and15_out, and16_out, and17_out,
       and18_out, and19_out, not_1_out, not_2_out, not_3_out, not_4_out, not_5_out, not_6_out;

  not not_1 (not_1_out, w);
  not not_2 (not_2_out, x);
  not not_3 (not_3_out, y);
  not not_4 (not_4_out, z);
  not not_5 (not_5_out, not_2_out);
  not not_6 (not_6_out, not_4_out);
  and and9 (and9_out, not_1_out, not_2_out);
  and and11 (and11_out, not_1_out, not_2_out);
  and and13 (and13_out, not_2_out, y);
  and and15 (and15_out, not_2_out, y);
  and and16 (and16_out, x, not_3_out);
  and and17 (and17_out, x, not_3_out);
  and and18 (and18_out, x, y);
  and and19 (and19_out, not_5_out, y);
  and and9_2 (out_13, w, not_4_out);
  and and20 (out_14, w, z);
  and and10 (and10_out, not_3_out, not_4_out);
  and and12 (and12_out, not_3_out, z);
  and and14 (and14_out, not_4_out, not_4_out);
  and and1 (out_5, and9_out, and10_out);
  and and2 (out_6, and11_out, and12_out);
  and and3 (out_7, and13_out, and14_out);
  and and4 (out_8, and15_out, z);
  and and5 (out_9, and16_out, not_4_out);
  and and6 (out_10, and17_out, z);
  and and7 (out_11, and18_out, not_4_out);
  and and8 (out_12, and19_out, not_6_out);
endmodule
