// Logisim project bcdToExcess3.circ as structural Verilog: 1 circuit, main circuit main
module main (
  input  _0,
  input  A,
  input  [2:0] BCD,
  output out_4,
  output out_5,
  output out_6,
  output out_7
);

  wire not_1_out, not_2_out;

  not not_1 (not_1_out, _0);
  not not_2 (not_2_out, A);
  Multiplexer #(.select(3)) multiplexer_1 (
    .in0(not_1_out), .in1(_0), .in2(_0), .in3(not_2_out), .in4(not_2_out), .in5(_0), .in6(_0),
    .in7(not_2_out), .out(out_6), .sel(BCD));  // open: en
  Multiplexer #(.select(3)) multiplexer_2 (
    .in0(not_1_out), .in1(_0), .in2(not_2_out), .in3(_0), .in4(not_2_out), .in5(_0), .in6(not_2_out),
    .in7(_0), .out(out_7), .sel(BCD));  // open: en
  Multiplexer #(.select(3)) multiplexer_3 (
    .in0(A), .in1(A), .in2(_0), .in3(_0), .in4(_0), .in5(not_2_out), .in6(not_2_out), .in7(not_2_out),
    .out(out_4), .sel(BCD));  // open: en
  Multiplexer #(.select(3)) multiplexer_4 (
    .in0(_0), .in1(not_1_out), .in2(not_2_out), .in3(not_2_out), .in4(not_2_out), .in5(_0), .in6(_0),
    .in7(_0), .out(out_5), .sel(BCD));  // open: en
endmodule
