// Logisim project johnson's counter.circ as structural Verilog: 1 circuit, main circuit main
module main (
  input  clear
);

  wire clock_out, d_ff_1_q, d_ff_2_q, d_ff_3_q, d_ff_4_qn;

  Clock clock (.out(clock_out));
  D_Flip_Flop d_ff_1 (.clk(clock_out), .D(d_ff_4_qn), .Q(d_ff_1_q), .reset(clear));  // open: Qn, preset, en
  D_Flip_Flop d_ff_2 (.clk(clock_out), .D(d_ff_1_q), .Q(d_ff_2_q), .reset(clear));  // open: Qn, preset, en
  D_Flip_Flop d_ff_3 (.clk(clock_out), .D(d_ff_2_q), .Q(d_ff_3_q), .reset(clear));  // open: Qn, preset, en
  D_Flip_Flop d_ff_4 (.clk(clock_out), .D(d_ff_3_q), .Qn(d_ff_4_qn), .reset(clear));  // open: Q, preset, en
endmodule
