// Logisim project look ahead carry.circ as structural Verilog: 4 circuits, main circuit Look-ahead Carry Generator
module Look_ahead_Carry_Generator (
  input  Ai,
  input  Bi,
  input  Ci,
  output Si,
  output Ci_2
);

  wire and_1_s, and_2_s, xor_1_xor;

  XOR xor_1 (.X(Ai), .Y(Bi), .XOR(xor_1_xor));
  AND and_1 (.X(Bi), .Y(Ai), .S(and_1_s));
  XOR xor_2 (.X(xor_1_xor), .Y(Ci), .XOR(Si));
  AND and_2 (.X(xor_1_xor), .Y(Ci), .S(and_2_s));
  OR or_1 (.X(and_2_s), .Y(and_1_s), .S(Ci_2));
endmodule

module XOR (
  input  X,
  input  Y,
  output XOR
);

  wire nand_1_out, nand_2_out, nand_3_out, nand_4_out;

  nand nand_1 (nand_1_out, X, X);
  nand nand_2 (nand_2_out, Y, Y);
  nand nand_3 (nand_3_out, nand_1_out, Y);
  nand nand_4 (nand_4_out, X, nand_2_out);
  nand nand_5 (XOR, nand_3_out, nand_4_out);
endmodule

module AND (
  input  X,
  input  Y,
  output S
);

  wire nand_1_out;

  nand nand_1 (nand_1_out, X, Y);
  nand nand_2 (S, nand_1_out, nand_1_out);
endmodule

module OR (
  input  X,
  input  Y,
  output S
);

  wire nand_1_out, nand_2_out;

  nand nand_1 (nand_1_out, X, X);
  nand nand_2 (nand_2_out, Y, Y);
  nand nand_3 (S, nand_1_out, nand_2_out);
endmodule
