// Logisim project magnitude comparator.circ as structural Verilog: 8 circuits, main circuit 3-input OR
module _3_bit_Magnitude_Comparator (
  input  [2:0] A,
  input  [2:0] B,
  output A___B,
  output A___B_2,
  output A___B_3
);

  wire and_1_s, and_2_s, and_3_s, and_4_s, and_5_s, and_6_s, and_7_s, and_8_s, n3_input_and_1_and,
       n3_input_and_2_and, nor_1_s, nor_2_s, nor_3_s, not_1_out, not_2_out, not_3_out, not_4_out, not_5_out,
       not_6_out;

  not not_1 (not_1_out, A[2]);
  not not_2 (not_2_out, B[2]);
  not not_3 (not_3_out, A[1]);
  not not_4 (not_4_out, B[1]);
  not not_5 (not_5_out, A[0]);
  not not_6 (not_6_out, B[0]);
  AND and_1 (.X(not_1_out), .Y(B[2]), .S(and_1_s));
  AND and_2 (.X(A[2]), .Y(not_2_out), .S(and_2_s));
  AND and_3 (.X(not_3_out), .Y(B[1]), .S(and_3_s));
  AND and_4 (.X(A[1]), .Y(not_4_out), .S(and_4_s));
  AND and_5 (.X(not_5_out), .Y(B[0]), .S(and_5_s));
  AND and_6 (.X(A[0]), .Y(not_6_out), .S(and_6_s));
  NOR nor_1 (.X(and_1_s), .Y(and_2_s), .S(nor_1_s));
  NOR nor_2 (.X(and_3_s), .Y(and_4_s), .S(nor_2_s));
  NOR nor_3 (.X(and_5_s), .Y(and_6_s), .S(nor_3_s));
  AND and_7 (.X(nor_1_s), .Y(and_3_s), .S(and_7_s));
  AND and_8 (.X(and_4_s), .Y(nor_1_s), .S(and_8_s));
  _3_input_AND u_3_input_and_1 (.A(nor_2_s), .B(and_5_s), .C(nor_1_s), .AND(n3_input_and_1_and));
  _3_input_AND u_3_input_and_2 (.A(nor_2_s), .B(and_6_s), .C(nor_1_s), .AND(n3_input_and_2_and));
  _3_input_OR u_3_input_or_1 (.A(and_1_s), .B(and_7_s), .C(n3_input_and_1_and), .OR(A___B));
  _3_input_OR u_3_input_or_2 (.A(and_2_s), .B(and_8_s), .C(n3_input_and_2_and), .OR(A___B_2));
  _3_input_AND u_3_input_and_3 (.A(nor_1_s), .B(nor_2_s), .C(nor_3_s), .AND(A___B_3));
endmodule

module XOR (
  input  X,
  input  Y,
  output XOR
);

  wire nand_1_out, nand_2_out, nand_3_out, nand_4_out;

  nand nand_1 (nand_1_out, X, X);
  nand nand_2 (nand_2_out, Y, Y);
  nand nand_3 (nand_3_out, nand_1_out, Y);
  nand nand_4 (nand_4_out, X, nand_2_out);
  nand nand_5 (XOR, nand_3_out, nand_4_out);
endmodule

module AND (
  input  X,
  input  Y,
  output S
);

  wire nand_1_out;

  nand nand_1 (nand_1_out, X, Y);
  nand nand_2 (S, nand_1_out, nand_1_out);
endmodule

module OR (
  input  X,
  input  Y,
  output S
);

  wire nand_1_out, nand_2_out;

  nand nand_1 (nand_1_out, X, X);
  nand nand_2 (nand_2_out, Y, Y);
  nand nand_3 (S, nand_1_out, nand_2_out);
endmodule

module NOR (
  input  X,
  input  Y,
  output S
);

  wire or_1_s;

  OR or_1 (.X(X), .Y(Y), .S(or_1_s));
  nand nand_1 (S, or_1_s, or_1_s);
endmodule

// OR
module _3_input_OR (
  input  A,
  input  B,
  input  C,
  output OR
);

  wire or_1_s;

  OR or_1 (.X(A), .Y(B), .S(or_1_s));
  OR or_2 (.X(or_1_s), .Y(C), .S(OR));
endmodule

// AND
module _3_input_AND (
  input  A,
  input  B,
  input  C,
  output AND
);

  wire and_1_s;

  AND and_1 (.X(A), .Y(B), .S(and_1_s));
  AND and_2 (.X(and_1_s), .Y(C), .S(AND));
endmodule

module exam (
);

  _3_bit_Magnitude_Comparator u_3_bit_magnitude_comparator_1 ();  // open: A, B, A___B, A___B_2, A___B_3
endmodule
