// Logisim project mod 5 counter.circ as structural Verilog: 1 circuit, main circuit main
module main (
  output Q0,
  output Q1,
  output Q2
);

  wire and_1_out, clock_out, not_1_out;

  Clock clock (.out(clock_out));
  J_K_Flip_Flop #(.trigger("falling")) j_k_ff_1 (
    .J(1'b1), .clk(clock_out), .K(1'b1), .Q(Q0), .reset(and_1_out));  // open: Qn, preset, en
  J_K_Flip_Flop #(.trigger("falling")) j_k_ff_2 (
    .J(1'b1), .clk(Q0), .K(1'b1), .Q(Q1), .reset(and_1_out));  // open: Qn, preset, en
  J_K_Flip_Flop #(.trigger("falling")) j_k_ff_3 (
    .J(1'b1), .clk(Q1), .K(1'b1), .Q(Q2), .reset(and_1_out));  // open: Qn, preset, en
  and and_1 (and_1_out, Q0, Q2);
  not not_1 (not_1_out, Q1);
endmodule
