// Logisim project modulo 6 counter.circ as structural Verilog: 1 circuit, main circuit main
module main (
  output Q1,
  output Q2,
  output Q3
);

  wire and_1_out, clock_1_out, not_1_out;

  Clock clock_1 (.out(clock_1_out));
  J_K_Flip_Flop #(.trigger("falling")) j_k_ff_1 (
    .J(1'b1), .clk(clock_1_out), .K(1'b1), .Q(Q1), .reset(and_1_out));  // open: Qn, preset, en
  J_K_Flip_Flop #(.trigger("falling")) j_k_ff_2 (
    .J(1'b1), .clk(Q1), .K(1'b1), .Q(Q2), .reset(and_1_out));  // open: Qn, preset, en
  J_K_Flip_Flop #(.trigger("falling")) j_k_ff_3 (
    .J(1'b1), .clk(Q2), .K(1'b1), .Q(Q3), .reset(and_1_out));  // open: Qn, preset, en
  not not_1 (not_1_out, Q1);
  and and_1 (and_1_out, not_1_out, Q2, Q3);
endmodule
