// Logisim project parallel adder.circ as structural Verilog: 4 circuits, main circuit main
module main (
  input  parallel_enable_out,
  input  B0,
  input  B1,
  input  B2,
  input  parallel_enable,
  input  clear,
  input  A0,
  input  A1,
  input  A2,
  output Q0,
  output Q1,
  output Q2
);

  wire and_1_out, and_2_out, and_3_out, and_4_out, and_5_out, and_6_out, and_7_out, clock_out,
       full_adder_1_ci, full_adder_1_si, full_adder_2_ci, full_adder_2_si, half_adder_1_carry,
       half_adder_1_sum, or_1_out, or_2_out, or_3_out, pipo_1_q0, pipo_1_q1, pipo_1_q2;

  and and_1 (and_1_out, parallel_enable_out, full_adder_1_ci);
  D_Flip_Flop d_ff_1 (.clk(clock_out), .D(and_1_out), .reset(clear));  // open: Q, Qn, preset, en
  Clock clock (.out(clock_out));
  full_adder full_adder_1 (
    .A(pipo_1_q2), .B(Q2), .C_i___1(full_adder_2_ci), .Si(full_adder_1_si), .Ci(full_adder_1_ci));
  full_adder full_adder_2 (
    .A(pipo_1_q1), .B(Q1), .C_i___1(half_adder_1_carry), .Si(full_adder_2_si), .Ci(full_adder_2_ci));
  pipo pipo_1 (
    .Parallel_enable(parallel_enable), .clk(clock_out), .clear(clear), .B2(B2), .Q2(pipo_1_q2), .B1(B1),
    .Q1(pipo_1_q1), .B0(B0), .Q0(pipo_1_q0));
  and and_2 (and_2_out, parallel_enable_out, half_adder_1_sum);
  or or_1 (or_1_out, and_2_out, and_4_out);
  pipo pipo_2 (
    .Parallel_enable(parallel_enable), .clk(clock_out), .clear(clear), .B2(or_2_out), .Q2(Q2), .B1(or_3_out),
    .Q1(Q1), .B0(or_1_out), .Q0(Q0));
  or or_2 (or_2_out, and_3_out, and_7_out);
  and and_3 (and_3_out, parallel_enable_out, full_adder_1_si);
  half_adder half_adder_1 (.A(pipo_1_q0), .B(Q0), .sum(half_adder_1_sum), .Carry(half_adder_1_carry));
  or or_3 (or_3_out, and_5_out, and_6_out);
  and and_4 (and_4_out, A0, parallel_enable);
  and and_5 (and_5_out, A1, parallel_enable);
  and and_6 (and_6_out, parallel_enable_out, full_adder_2_si);
  and and_7 (and_7_out, A2, parallel_enable);
endmodule

module half_adder (
  input  A,
  input  B,
  output sum,
  output Carry
);

  xor xor_1 (sum, A, B);
  and and_1 (Carry, A, B);
endmodule

module full_adder (
  input  A,
  input  B,
  input  C_i___1,
  output Si,
  output Ci
);

  wire half_adder_1_carry, half_adder_1_sum, half_adder_2_carry;

  half_adder half_adder_1 (.A(A), .B(B), .sum(half_adder_1_sum), .Carry(half_adder_1_carry));
  half_adder half_adder_2 (.A(half_adder_1_sum), .B(C_i___1), .sum(Si), .Carry(half_adder_2_carry));
  or or_1 (Ci, half_adder_1_carry, half_adder_2_carry);
endmodule

module pipo (
  input  Parallel_enable,
  input  B2,
  input  B0,
  input  B1,
  input  clk,
  input  clear,
  output Q2,
  output Q1,
  output Q0
);

  wire and_1_out, and_2_out, and_3_out;

  and and_1 (and_1_out, B2, Parallel_enable);
  D_Flip_Flop #(.trigger("falling")) d_ff_1 (.clk(clk), .D(and_1_out), .Q(Q2), .reset(clear));  // open: Qn, preset, en
  and and_2 (and_2_out, Parallel_enable, B1);
  D_Flip_Flop d_ff_2 (.clk(clk), .D(and_2_out), .Q(Q1), .reset(clear));  // open: Qn, preset, en
  and and_3 (and_3_out, B0, Parallel_enable);
  D_Flip_Flop d_ff_3 (.clk(clk), .D(and_3_out), .Q(Q0), .reset(clear));  // open: Qn, preset, en
endmodule
