// Logisim project piso register.circ as structural Verilog: 1 circuit, main circuit main
module main (
  input  B0,
  input  B1,
  input  B2,
  input  B3,
  input  load_shift,
  input  clear,
  input  clock,
  output serial_out
);

  wire and_1_out, and_2_out, and_3_out, and_4_out, and_5_out, and_6_out, d_ff_1_q, d_ff_2_q, d_ff_3_q,
       not_1_out, or_1_out, or_2_out, or_3_out;

  not not_1 (not_1_out, load_shift);
  and and_1 (and_1_out, load_shift, B1);
  D_Flip_Flop #(.trigger("falling")) d_ff_1 (.clk(clock), .D(B0), .Q(d_ff_1_q), .reset(clear));  // open: Qn, preset, en
  and and_2 (and_2_out, d_ff_1_q, not_1_out);
  or or_1 (or_1_out, and_1_out, and_2_out);
  D_Flip_Flop #(.trigger("falling")) d_ff_2 (
    .clk(clock), .D(or_1_out), .Q(d_ff_2_q), .reset(clear));  // open: Qn, preset, en
  and and_3 (and_3_out, load_shift, B2);
  and and_4 (and_4_out, d_ff_2_q, not_1_out);
  or or_2 (or_2_out, and_3_out, and_4_out);
  D_Flip_Flop #(.trigger("falling")) d_ff_3 (
    .clk(clock), .D(or_2_out), .Q(d_ff_3_q), .reset(clear));  // open: Qn, preset, en
  and and_5 (and_5_out, load_shift, B3);
  and and_6 (and_6_out, d_ff_3_q, not_1_out);
  or or_3 (or_3_out, and_5_out, and_6_out);
  D_Flip_Flop #(.trigger("falling")) d_ff_4 (
    .clk(clock), .D(or_3_out), .Q(serial_out), .reset(clear));  // open: Qn, preset, en
endmodule
