// Logisim project prac1.circ as structural Verilog: 1 circuit, main circuit main
module main (
  output Q1,
  output Q2,
  output Q3
);

  wire clock_out, not_1_out;

  Clock clock (.out(clock_out));
  T_Flip_Flop #(.trigger("falling")) t_ff_1 (.clk(clock_out), .T(not_1_out), .Q(Q1));  // open: Qn, preset, reset, en
  not not_1 (not_1_out, Q1);
  T_Flip_Flop #(.trigger("falling")) t_ff_2 (.clk(clock_out), .T(Q1), .Q(Q2));  // open: Qn, preset, reset, en
  T_Flip_Flop t_ff_3 (.clk(clock_out), .T(Q2), .Q(Q3));  // open: Qn, preset, reset, en
endmodule
