// Logisim project prac2.circ as structural Verilog: 1 circuit, main circuit main
module main (
  output Q0,
  output Q1,
  output Q2,
  output Q3
);

  wire and_1_out, and_2_out, and_3_out, and_4_out, and_5_out, and_6_out, and_7_out, and_8_out, clock_out,
       not_1_out, not_2_out, not_3_out, not_4_out, not_5_out, not_6_out, or_1_out, or_2_out, t_ff_1_qn,
       t_ff_2_qn;

  Clock clock (.out(clock_out));
  T_Flip_Flop t_ff_1 (.clk(clock_out), .T(and_1_out), .Q(Q0), .Qn(t_ff_1_qn));  // open: preset, reset, en
  not not_1 (not_1_out, Q0);
  and and_1 (and_1_out, not_6_out, not_3_out, t_ff_2_qn);
  T_Flip_Flop t_ff_2 (.clk(clock_out), .T(and_5_out), .Q(Q1), .Qn(t_ff_2_qn));  // open: preset, reset, en
  T_Flip_Flop t_ff_3 (.clk(clock_out), .T(and_6_out), .Q(Q2));  // open: Qn, preset, reset, en
  and and_2 (and_2_out, t_ff_2_qn, t_ff_1_qn, or_1_out);
  or or_1 (or_1_out, and_8_out, and_7_out);
  not not_2 (not_2_out, Q1);
  and and_3 (and_3_out, not_2_out, Q2);
  not not_3 (not_3_out, Q2);
  T_Flip_Flop t_ff_4 (.clk(clock_out), .T(and_2_out), .Q(Q3));  // open: Qn, preset, reset, en
  and and_4 (and_4_out, Q1, not_3_out);
  not not_4 (not_4_out, Q0);
  not not_5 (not_5_out, Q3);
  and and_5 (and_5_out, not_5_out, not_4_out, or_2_out);
  or or_2 (or_2_out, and_4_out, and_3_out);
  not not_6 (not_6_out, Q3);
  and and_6 (and_6_out, not_1_out, not_6_out, Q2);
  and and_7 (and_7_out, not_6_out, Q2);
  and and_8 (and_8_out, Q3, not_3_out);
endmodule
