// Logisim project prac3.circ as structural Verilog: 2 circuits, main circuit main
module main (
  input  A3,
  input  B3,
  input  A2,
  input  B2,
  input  A1,
  input  B1,
  input  A0,
  input  B0,
  output A___B,
  output A___B_2,
  output A___B_3
);

  wire and_1_out, and_2_out, and_3_out, and_4_out, and_5_out, and_6_out, and_7_out, and_8_out, and_9_out,
       and_10_out, and_11_out, and_12_out, and_13_out, and_14_out, nor_1_out, nor_2_out, nor_3_out,
       nor_4_out, not_1_out, not_2_out, not_3_out, not_4_out, not_5_out, not_6_out, not_7_out, not_8_out;

  not not_1 (not_1_out, A3);
  and and_1 (and_1_out, not_1_out, B3);
  and and_2 (and_2_out, A3, not_2_out);
  not not_2 (not_2_out, B3);
  not not_3 (not_3_out, A2);
  and and_3 (and_3_out, not_3_out, B2);
  and and_4 (and_4_out, A2, not_4_out);
  not not_4 (not_4_out, B2);
  not not_5 (not_5_out, A1);
  and and_5 (and_5_out, not_5_out, B1);
  and and_6 (and_6_out, A1, not_6_out);
  not not_6 (not_6_out, B1);
  not not_7 (not_7_out, A0);
  and and_7 (and_7_out, not_7_out, B0);
  and and_8 (and_8_out, A0, not_8_out);
  not not_8 (not_8_out, B0);
  nor nor_1 (nor_1_out, and_1_out, and_2_out);
  nor nor_2 (nor_2_out, and_3_out, and_4_out);
  nor nor_3 (nor_3_out, and_5_out, and_6_out);
  nor nor_4 (nor_4_out, and_7_out, and_8_out);
  and and_9 (and_9_out, nor_1_out, nor_2_out, and_5_out);
  and and_10 (and_10_out, and_4_out, nor_2_out);
  and and_11 (and_11_out, nor_2_out, and_6_out, nor_1_out);
  and and_12 (and_12_out, nor_1_out, nor_2_out, nor_3_out, and_7_out);
  and and_13 (and_13_out, and_8_out, nor_1_out, nor_2_out, nor_3_out);
  and and_14 (and_14_out, and_3_out, nor_1_out);
  or or_1 (A___B, and_1_out, and_14_out, and_9_out, and_12_out);
  or or_2 (A___B_2, and_2_out, and_10_out, and_11_out, and_13_out);
  and and_15 (A___B_3, nor_1_out, nor_2_out, nor_3_out, nor_4_out);
endmodule

module compare (
  input  [3:0] X,
  input  [3:0] N,
  input  [3:0] Y,
  output Ans
);

  wire main_1_a___b, main_2_a___b_2;

  main main_1 (
    .A3(N[3]), .B3(X[3]), .A2(N[2]), .B2(X[2]), .A1(N[1]), .B1(X[1]), .A0(N[0]), .B0(X[0]),
    .A___B(main_1_a___b));  // open: A___B_2, A___B_3
  main main_2 (
    .A3(N[3]), .B3(Y[3]), .A2(N[2]), .B2(Y[2]), .A1(N[1]), .B1(Y[1]), .A0(N[0]), .B0(Y[0]),
    .A___B_2(main_2_a___b_2));  // open: A___B, A___B_3
  or or_1 (Ans, main_1_a___b, main_2_a___b_2);
endmodule
