// Logisim project serial adder last try.circ as structural Verilog: 3 circuits, main circuit main
module main (
  input  A0,
  input  A1,
  input  A2,
  input  parallel_enable_in,
  input  serial_in,
  input  B2,
  input  B1,
  input  B0
);

  wire and_1_out, and_2_out, and_3_out, and_4_out, and_5_out, and_6_out, and_7_out, and_8_out, and_9_out,
       and_10_out, and_11_out, and_12_out, clock_out, d_ff_1_q, d_ff_2_q, d_ff_3_q, d_ff_4_q, d_ff_5_q,
       d_ff_6_q, d_ff_7_q, full_adder_1_carry, full_adder_1_sum, or_1_out, or_2_out, or_3_out, or_4_out,
       or_5_out, or_6_out;

  Clock clock (.out(clock_out));
  and and_1 (and_1_out, A2, parallel_enable_in);
  and and_2 (and_2_out, serial_in, full_adder_1_sum);
  or or_1 (or_1_out, and_1_out, and_2_out);
  and and_3 (and_3_out, serial_in, d_ff_6_q);
  and and_4 (and_4_out, parallel_enable_in, B2);
  D_Flip_Flop d_ff_1 (.clk(clock_out), .D(or_1_out), .Q(d_ff_1_q));  // open: Qn, preset, en, reset
  D_Flip_Flop d_ff_2 (.clk(clock_out), .D(or_2_out), .Q(d_ff_2_q));  // open: Qn, preset, en, reset
  or or_2 (or_2_out, and_3_out, and_4_out);
  and and_5 (and_5_out, A1, parallel_enable_in);
  or or_3 (or_3_out, and_5_out, and_6_out);
  and and_6 (and_6_out, serial_in, d_ff_1_q);
  and and_7 (and_7_out, serial_in, d_ff_2_q);
  or or_4 (or_4_out, and_7_out, and_8_out);
  and and_8 (and_8_out, parallel_enable_in, B1);
  D_Flip_Flop d_ff_3 (.clk(clock_out), .D(or_3_out), .Q(d_ff_3_q));  // open: Qn, preset, en, reset
  D_Flip_Flop d_ff_4 (.clk(clock_out), .D(or_4_out), .Q(d_ff_4_q));  // open: Qn, preset, en, reset
  and and_9 (and_9_out, A0, parallel_enable_in);
  and and_10 (and_10_out, serial_in, d_ff_3_q);
  or or_5 (or_5_out, and_9_out, and_10_out);
  and and_11 (and_11_out, serial_in, d_ff_4_q);
  or or_6 (or_6_out, and_11_out, and_12_out);
  and and_12 (and_12_out, parallel_enable_in, B0);
  D_Flip_Flop d_ff_5 (.clk(clock_out), .D(or_5_out), .Q(d_ff_5_q));  // open: Qn, preset, en, reset
  D_Flip_Flop d_ff_6 (.clk(clock_out), .D(or_6_out), .Q(d_ff_6_q));  // open: Qn, preset, en, reset
  full_adder full_adder_1 (
    .Ai(d_ff_5_q), .Bi(d_ff_6_q), .C_i___1(d_ff_7_q), .sum(full_adder_1_sum), .carry(full_adder_1_carry));
  D_Flip_Flop d_ff_7 (.clk(clock_out), .D(full_adder_1_carry), .Q(d_ff_7_q));  // open: Qn, preset, en, reset
endmodule

module half_adder (
  input  A,
  input  B,
  output sum,
  output carry
);

  xor xor_1 (sum, A, B);
  and and_1 (carry, A, B);
endmodule

module full_adder (
  input  Ai,
  input  Bi,
  input  C_i___1,
  output sum,
  output carry
);

  wire half_adder_1_carry, half_adder_1_sum;

  half_adder half_adder_1 (.A(Ai), .B(Bi), .sum(half_adder_1_sum), .carry(half_adder_1_carry));
  half_adder half_adder_2 (.A(half_adder_1_sum), .B(C_i___1), .sum(sum));  // open: carry
  or or_1 (carry, half_adder_1_carry, C_i___1);
endmodule
